# Fritzing sketch live temperature (saved by Fritzing 0.9.3b)
circuit board: 8.46667cm x 5.64444cm
breadboards: 1

parts:
  Gizwits_WiFi_Witty_ESP-12F1 = Gizwits WiFi Witty ESP-12F
  DHT1 = Humidity and Temperature Sensor DHT11

nets:
  VCC: Gizwits_WiFi_Witty_ESP-12F1.VCC, DHT1.Vcc
  N1: Gizwits_WiFi_Witty_ESP-12F1.GND, DHT1.GND_2
  N2: Gizwits_WiFi_Witty_ESP-12F1.GPIO5, DHT1.Data-signal

custom parts:
  Humidity and Temperature Sensor DHT11: Digital relative humidity & temperature sensor DHT11
